# Fritzing sketch Pool-Control (saved by Fritzing 0.9.3b)
circuit board: 5.92561cm x 5.10948cm
breadboards: 1

parts:
  R1 = Resistor [tolerance=±5% resistance=4.7k package=THT]
  DS2 = DS18B20 1-Wire Temperature Sensor Probe Cable
  U3 = ESP32S-HiLetgo [part_number=ESP32S-HiLetgo]
  DS3 = DS18B20 1-Wire Temperature Sensor Probe Cable
  R2 = Resistor [tolerance=±5% resistance=4.7k package=THT]
  U2 = RF-LINK_TX [package=rf-link_tx]

nets:
  VDD: R1.Pin_0, DS2.VDD, U3.3.3, DS3.VDD, R2.Pin_0, U2.+5V
  N1: R1.Pin_1, DS2.DQ, U3.GPIO17
  GND: DS2.GND, U3.GND, DS3.GND, U2.GND
  N2: U3.GPIO16, DS3.DQ, R2.Pin_1
  N3: U3.GPIO18, U2.DATA

notes:
  Pool-Controller
  Solar
  Pool
  433MHz Sender

custom parts:
  ESP32S-HiLetgo: HiLetgo ESP-WROOM-32 ESP32 ESP-32S Development Board 2.4GHz Dual-Mode WiFi + Bluetooth Dual Cores Microcontroller The ESP32 integrated with Antenna switches, RF Balun, power amplifiers, low-noise amplifiers, filters, and management modules, and the entire solution occupies the least area of PCB. 2.4 GHz Wi-Fi plus Bluetooth dual-mode chip, with TSMC Ultra-low power consumption 40nm technology,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
